# Fritzing sketch Wiring (saved by Fritzing 0.9.2b)
perfboards: 1

parts:
  IC1 = PICAXE-20M [package=THT]
  JP2 = Header 1 [package=1x01_offset]
  JP3 = Header 1 [package=1x01_offset]
  JP4 = Header 1 [package=1x01_offset]
  JP6 = Header 1 [package=1x01_offset]
  JP7 = Header 1 [package=1x01_offset]
  JP8 = Header 1 [package=1x01_offset]
  JP9 = Header 1 [package=1x01_offset]
  JP10 = Header 1 [package=1x01_offset]
  BAT2 = BC9VPC [package=bc9vpc]
  Bauteil1 = Dual H-Bridge L298
  JP11 = Header 1 [package=1x01_offset]
  JP12 = Header 1 [package=1x01_offset]
  JP13 = Header 1 [package=1x01_offset]
  J2 = Basic Servo
  JP14 = Header 12 [package=1x12_machine-pin-header_lock.004]
  LED6 = RGB LED (com. cathode, rgb) [package="5 mm [THT]"]
  LED7 = LED - 5mm [color="Red (633nm)" package="5 mm [THT]"]
  LED8 = LED - 5mm [color="Red (633nm)" package="5 mm [THT]"]
  LED9 = LED - 5mm [color="Red (633nm)" package="5 mm [THT]"]
  LED10 = LED - 5mm [color="Red (633nm)" package="5 mm [THT]"]
  R17 = Resistor [tolerance=±5% resistance=1k package="0805 [SMD]"]
  R18 = Resistor [tolerance=±5% resistance=1k package="0805 [SMD]"]
  R19 = Resistor [tolerance=±5% resistance=1k package="0805 [SMD]"]
  R20 = Resistor [tolerance=±5% resistance=1k package="0805 [SMD]"]
  R21 = Resistor [tolerance=±5% resistance=1k package="0805 [SMD]"]
  R22 = Resistor [tolerance=±5% resistance=1k package="0805 [SMD]"]
  R23 = Resistor [tolerance=±5% resistance=1k package="0805 [SMD]"]
  JP16 = Header 10 [package=1x10-2mm-smd]
  R24 = Resistor [tolerance=±5% resistance=47k package="0805 [SMD]"]
  R25 = Resistor [tolerance=±5% resistance=47k package="0805 [SMD]"]
  R26 = Resistor [tolerance=±5% resistance=47k package="0805 [SMD]"]
  R27 = Resistor [tolerance=±5% resistance=47k package="0805 [SMD]"]
  R28 = Resistor [tolerance=±5% resistance=47k package="0805 [SMD]"]
  R29 = Resistor [tolerance=±5% resistance=47k package="0805 [SMD]"]
  R30 = Resistor [tolerance=±5% resistance=47k package="0805 [SMD]"]
  R31 = Resistor [tolerance=±5% resistance=47k package="0805 [SMD]"]
  R32 = Resistor [tolerance=±5% resistance=47k package="0805 [SMD]"]
  M2 = DC Motor
  Raspberry_Pi1 = Raspberry Pi 2
  PART1 = SparkFun Block for Intel Edison - GPIO [part_number=DEV-13038]
  U2 = EDISON  # not connected
  UDN_2981_-_8-Channel_Source_Driver1 = DIP - 18 pins [package="DIP (Dual Inline) [THT]"]  # not connected

nets:
  N1: IC1.+V, JP9.1, Bauteil1.IN1, JP12.1, J2.vcc
  GND: IC1.Serial_In, IC1.Serial_Out, IC1.0V, JP2.1, JP3.1, BAT2.V-, Bauteil1.GND, JP11.1, J2.gnd, JP14.2, JP14.4, JP14.6, JP14.8, JP14.11, LED6.common_cathode, LED7.cathode, LED8.cathode, LED9.cathode, LED10.cathode, JP16.1, R24.Pin_1, R25.Pin_1, R26.Pin_1, R27.Pin_1, R28.Pin_1, R29.Pin_1, R30.Pin_1, R31.Pin_1, R32.Pin_1, Raspberry_Pi1.GND, PART1.GND
  N2: IC1.In_7_/_ADC_7, JP16.10, R24.Pin_0, Raspberry_Pi1.GPIO12, PART1.GP12
  N3: IC1.In_6, JP16.9, R25.Pin_0, Raspberry_Pi1.GPIO16, PART1.GP15
  N4: IC1.In_5, JP16.7, R27.Pin_0, Raspberry_Pi1.GPIO13, PART1.GP13
  N5: IC1.In_4, JP16.6, R28.Pin_0, Raspberry_Pi1.GPIO17, PART1.GP46
  N6: IC1.In_3_/_ADC_3, JP16.5, R29.Pin_0, Raspberry_Pi1.GPIO27, PART1.GP47
  N7: IC1.In_2_/_ADC_2, JP16.4, R30.Pin_0, Raspberry_Pi1.GPIO22, PART1.GP48
  N8: IC1.In_1_/_ADC_1, JP16.3, R31.Pin_0, Raspberry_Pi1.GPIO10, PART1.GP45
  N9: IC1.In_0_/_Infrain, JP16.2, R32.Pin_0, Raspberry_Pi1.GPIO9, PART1.GP44
  N10: IC1.Out_7, R22.Pin_0, R23.Pin_0
  N11: IC1.Out_6, R20.Pin_0, R21.Pin_0
  N12: IC1.Out_5, R19.Pin_0
  N13: IC1.Out_4, R18.Pin_0
  N14: IC1.Out_3, R17.Pin_0
  N15: IC1.Out_2, JP13.1, J2.pulse
  N16: IC1.Out_1, JP8.1, Bauteil1.IN2
  N17: IC1.Out_0_/_Infraout, JP10.1, Bauteil1.ENA
  N18: JP4.1, JP6.1, BAT2.V+, Bauteil1.VMS
  5V: JP7.1, Bauteil1.5V, Bauteil1.+5V, JP16.8, R26.Pin_0, Raspberry_Pi1.GPIO20, PART1.GP14
  N19: Bauteil1.MOTORA1, M2.pin_1
  N20: Bauteil1.MOTORA2, M2.pin_2
  N21: JP14.1, LED10.anode, R23.Pin_1
  N22: JP14.3, LED9.anode, R22.Pin_1
  N23: JP14.5, LED8.anode, R21.Pin_1
  N24: JP14.7, LED7.anode, R20.Pin_1
  N25: JP14.9, LED6.blue_anode, R19.Pin_1
  N26: JP14.10, LED6.green_anode, R18.Pin_1
  N27: JP14.12, LED6.red_anode, R17.Pin_1

notes:
  PICAXE = 74AC541

custom parts:
  Dual H-Bridge L298: Description:The L298N driver module, using ST's L298N chip can directly drive two 3-30V DC motor, and provides a 5V output interface can 5V single-chip circuitry to supply, support 3.3VMCU control, you can easily control the DC motor speed and direction, you can also control the 2-phase stepper motor, smart car essential. Features: Driver: L298N Dual H Bridge DC Motor Driver IC Driven part of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
  SparkFun Block for Intel Edison - GPIO: The Intel® Edison is an ultra small computing platform that will change the way you look at embedded electronics. Each Edison is packed with a huge amount of tech goodies into a tiny package while still providing the same robust strength of your go-to single board computer. Powered by the Intel® Atom™ SoC dual-core CPU and including an integrated WiFi, Bluetooth LE, and a 70-pin connector to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
  DIP - 18 pins: Recommended for high-side switching applications that benefit from separate logic and load grounds, these devices encompass load supply voltages to 50 V and output currents to -500 mA. These 8-channel source drivers are useful for interfacing between low-level logic and high-current loads. Typical loads include relays, solenoids, lamps, stepper and/or servo motors, print hammers, and LEDs.
